// Logisim project schemas.circ as structural Verilog: 1 circuit, main circuit main
module main (
  input  LSB,
  input  in_2,
  input  in_3,
  input  MSB,
  input  enable,
  input  clock,
  input  reset_n,
  input  LSB_2,
  input  in_9,
  input  in_10,
  input  MSB_2,
  input  LSB_3,
  input  in_13,
  input  in_14,
  input  MSB_3
);

  wire and_1_out, and_2_out, and_3_out, and_4_out, and_5_out, and_6_out, and_7_out, and_8_out, and_9_out,
       and_10_out, and_11_out, and_12_out, and_13_out, and_14_out, and_15_out, and_16_out, and_17_out,
       and_18_out, and_19_out, and_20_out, and_21_out, and_22_out, and_23_out, and_24_out, and_25_out,
       and_26_out, and_27_out, and_28_out, and_29_out, and_30_out, and_31_out, and_32_out, and_33_out,
       and_34_out, and_35_out, and_36_out, and_37_out, and_38_out, and_39_out, and_40_out, and_41_out,
       and_42_out, and_43_out, and_44_out, and_45_out, nor_1_out, nor_2_out, nor_3_out, nor_4_out, nor_5_out,
       nor_6_out, nor_7_out, nor_8_out, nor_9_out, nor_10_out, nor_11_out, nor_12_out, nor_13_out,
       nor_14_out, nor_15_out, nor_16_out, nor_17_out, nor_18_out, nor_19_out, nor_20_out, nor_21_out,
       nor_22_out, nor_23_out, nor_24_out, not_1_out, not_2_out, not_3_out, not_4_out, not_5_out, not_6_out,
       not_7_out, not_8_out, not_9_out, not_10_out, not_11_out, not_12_out, not_13_out, not_14_out,
       not_15_out, not_16_out, not_17_out, not_18_out, not_19_out, not_20_out, register_1_q, register_2_q,
       register_3_q, register_4_q, register_5_q, register_6_q, register_7_q, register_8_q, register_9_q,
       register_10_q, register_11_q, register_12_q, register_13_q, register_14_q, register_15_q,
       register_16_q, xnor_1_out, xnor_2_out, xnor_3_out, xnor_4_out;

  not not_1 (not_1_out, register_4_q);
  Register #(.width(1)) register_1 (.D(LSB), .en(enable), .clk(clock), .Q(register_1_q), .clr(reset_n));
  Register #(.width(1)) register_2 (.D(in_2), .en(enable), .clk(clock), .Q(register_2_q), .clr(reset_n));
  Register #(.width(1)) register_3 (.D(in_3), .en(enable), .clk(clock), .Q(register_3_q), .clr(reset_n));
  Register #(.width(1)) register_4 (.D(MSB), .en(enable), .clk(clock), .Q(register_4_q), .clr(reset_n));
  not not_2 (not_2_out, register_3_q);
  not not_3 (not_3_out, register_2_q);
  not not_4 (not_4_out, register_1_q);
  Register #(.width(1)) register_5 (.D(register_1_q), .en(enable), .clk(clock), .Q(register_5_q), .clr(reset_n));
  Register #(.width(1)) register_6 (.D(register_2_q), .en(enable), .clk(clock), .Q(register_6_q), .clr(reset_n));
  Register #(.width(1)) register_7 (.D(register_3_q), .en(enable), .clk(clock), .Q(register_7_q), .clr(reset_n));
  Register #(.width(1)) register_8 (.D(register_4_q), .en(enable), .clk(clock), .Q(register_8_q), .clr(reset_n));
  and and_1 (and_1_out, not_1_out, not_2_out, not_3_out, register_1_q);
  and and_2 (and_2_out, register_3_q, not_3_out, not_4_out);
  and and_3 (and_3_out, register_3_q, not_3_out, register_1_q);
  and and_4 (and_4_out, register_3_q, register_2_q, not_4_out);
  and and_5 (and_5_out, not_2_out, register_2_q, not_4_out);
  and and_6 (and_6_out, register_3_q, register_2_q, register_1_q);
  and and_7 (and_7_out, not_3_out, register_3_q);
  and and_8 (and_8_out, not_1_out, not_2_out, register_1_q);
  and and_9 (and_9_out, register_2_q, not_2_out);
  and and_10 (and_10_out, register_2_q, register_1_q);
  and and_11 (and_11_out, not_3_out, not_2_out, not_1_out);
  Register #(.width(1)) register_9 (.D(register_5_q), .en(enable), .clk(clock), .Q(register_9_q), .clr(reset_n));
  Register #(.width(1)) register_10 (.D(register_6_q), .en(enable), .clk(clock), .Q(register_10_q), .clr(reset_n));
  Register #(.width(1)) register_11 (.D(register_7_q), .en(enable), .clk(clock), .Q(register_11_q), .clr(reset_n));
  Register #(.width(1)) register_12 (.D(register_8_q), .en(enable), .clk(clock), .Q(register_12_q), .clr(reset_n));
  Register #(.width(1)) register_13 (.D(register_9_q), .en(enable), .clk(clock), .Q(register_13_q), .clr(reset_n));
  Register #(.width(1)) register_14 (.D(register_10_q), .en(enable), .clk(clock), .Q(register_14_q), .clr(reset_n));
  Register #(.width(1)) register_15 (.D(register_11_q), .en(enable), .clk(clock), .Q(register_15_q), .clr(reset_n));
  Register #(.width(1)) register_16 (.D(register_12_q), .en(enable), .clk(clock), .Q(register_16_q), .clr(reset_n));
  nor nor_1 (nor_1_out, and_1_out, and_2_out);
  nor nor_2 (nor_2_out, and_3_out, and_4_out);
  not not_5 (not_5_out, and_5_out);
  nor nor_3 (nor_3_out, and_2_out, and_1_out, and_6_out);
  nor nor_4 (nor_4_out, and_7_out, register_1_q);
  nor nor_5 (nor_5_out, and_8_out, and_9_out, and_10_out);
  nor nor_6 (nor_6_out, and_6_out, and_11_out);
  _7_Segment_Display u_7_segment_display_1 (
    .g(nor_6_out), .f(nor_5_out), .a(nor_1_out), .b(nor_2_out), .e(nor_4_out), .d(nor_3_out), .c(not_5_out));  // open: dp
  xnor xnor_1 (xnor_1_out, LSB_2, LSB_3);
  xnor xnor_2 (xnor_2_out, in_9, in_13);
  xnor xnor_3 (xnor_3_out, in_10, in_14);
  xnor xnor_4 (xnor_4_out, MSB_2, MSB_3);
  not not_6 (not_6_out, register_8_q);
  not not_7 (not_7_out, register_12_q);
  not not_8 (not_8_out, register_16_q);
  not not_9 (not_9_out, register_7_q);
  not not_10 (not_10_out, register_6_q);
  not not_11 (not_11_out, register_11_q);
  not not_12 (not_12_out, register_10_q);
  not not_13 (not_13_out, register_15_q);
  not not_14 (not_14_out, register_14_q);
  and and_12 (and_12_out, xnor_1_out, xnor_2_out, xnor_3_out, xnor_4_out);
  not not_15 (not_15_out, register_5_q);
  not not_16 (not_16_out, register_9_q);
  not not_17 (not_17_out, register_13_q);
  and and_13 (and_13_out, not_6_out, not_9_out, not_10_out, register_5_q);
  and and_14 (and_14_out, register_7_q, not_10_out, not_15_out);
  and and_15 (and_15_out, register_7_q, not_10_out, register_5_q);
  and and_16 (and_16_out, register_7_q, register_6_q, not_15_out);
  and and_17 (and_17_out, not_9_out, register_6_q, not_15_out);
  and and_18 (and_18_out, register_7_q, register_6_q, register_5_q);
  and and_19 (and_19_out, not_10_out, register_7_q);
  and and_20 (and_20_out, not_6_out, not_9_out, register_5_q);
  and and_21 (and_21_out, register_6_q, not_9_out);
  and and_22 (and_22_out, register_6_q, register_5_q);
  and and_23 (and_23_out, not_10_out, not_9_out, not_6_out);
  and and_24 (and_24_out, not_7_out, not_11_out, not_12_out, register_9_q);
  and and_25 (and_25_out, register_11_q, not_12_out, not_16_out);
  and and_26 (and_26_out, register_11_q, not_12_out, register_9_q);
  and and_27 (and_27_out, register_11_q, register_10_q, not_16_out);
  and and_28 (and_28_out, not_11_out, register_10_q, not_16_out);
  and and_29 (and_29_out, register_11_q, register_10_q, register_9_q);
  and and_30 (and_30_out, not_12_out, register_11_q);
  and and_31 (and_31_out, not_7_out, not_11_out, register_9_q);
  and and_32 (and_32_out, register_10_q, not_11_out);
  and and_33 (and_33_out, register_10_q, register_9_q);
  and and_34 (and_34_out, not_12_out, not_11_out, not_7_out);
  and and_35 (and_35_out, not_8_out, not_13_out, not_14_out, register_13_q);
  and and_36 (and_36_out, register_15_q, not_14_out, not_17_out);
  and and_37 (and_37_out, register_15_q, not_14_out, register_13_q);
  and and_38 (and_38_out, register_15_q, register_14_q, not_17_out);
  and and_39 (and_39_out, not_13_out, register_14_q, not_17_out);
  and and_40 (and_40_out, register_15_q, register_14_q, register_13_q);
  and and_41 (and_41_out, not_14_out, register_15_q);
  and and_42 (and_42_out, not_8_out, not_13_out, register_13_q);
  and and_43 (and_43_out, register_14_q, not_13_out);
  and and_44 (and_44_out, register_14_q, register_13_q);
  and and_45 (and_45_out, not_14_out, not_13_out, not_8_out);
  nor nor_7 (nor_7_out, and_13_out, and_14_out);
  nor nor_8 (nor_8_out, and_15_out, and_16_out);
  not not_18 (not_18_out, and_17_out);
  nor nor_9 (nor_9_out, and_14_out, and_13_out, and_18_out);
  nor nor_10 (nor_10_out, and_19_out, register_5_q);
  nor nor_11 (nor_11_out, and_20_out, and_21_out, and_22_out);
  nor nor_12 (nor_12_out, and_18_out, and_23_out);
  nor nor_13 (nor_13_out, and_24_out, and_25_out);
  nor nor_14 (nor_14_out, and_26_out, and_27_out);
  not not_19 (not_19_out, and_28_out);
  nor nor_15 (nor_15_out, and_25_out, and_24_out, and_29_out);
  nor nor_16 (nor_16_out, and_30_out, register_9_q);
  nor nor_17 (nor_17_out, and_31_out, and_32_out, and_33_out);
  nor nor_18 (nor_18_out, and_29_out, and_34_out);
  nor nor_19 (nor_19_out, and_35_out, and_36_out);
  nor nor_20 (nor_20_out, and_37_out, and_38_out);
  not not_20 (not_20_out, and_39_out);
  nor nor_21 (nor_21_out, and_36_out, and_35_out, and_40_out);
  nor nor_22 (nor_22_out, and_41_out, register_13_q);
  nor nor_23 (nor_23_out, and_42_out, and_43_out, and_44_out);
  nor nor_24 (nor_24_out, and_40_out, and_45_out);
  _7_Segment_Display u_7_segment_display_2 (
    .g(nor_12_out), .f(nor_11_out), .a(nor_7_out), .b(nor_8_out), .e(nor_10_out), .d(nor_9_out),
    .c(not_18_out));  // open: dp
  _7_Segment_Display u_7_segment_display_3 (
    .g(nor_18_out), .f(nor_17_out), .a(nor_13_out), .b(nor_14_out), .e(nor_16_out), .d(nor_15_out),
    .c(not_19_out));  // open: dp
  _7_Segment_Display u_7_segment_display_4 (
    .g(nor_24_out), .f(nor_23_out), .a(nor_19_out), .b(nor_20_out), .e(nor_22_out), .d(nor_21_out),
    .c(not_20_out));  // open: dp

  // Notes on the sheet:
  //   Switchs externes
  //   Sortie 1
  //   Sortie 2
  //   Signal de référence
  //   Signal à comparer
  //   Sortie 3
  //   Sortie 4
endmodule
